# Fritzing sketch LDR Array-v1 (saved by Fritzing 1.0.1rc)
circuit board: 2.40639cm x 2.78902cm
breadboards: 1

parts:
  l_u_+_o_r = female pin header, 5 pins [form="♀ (female)"]
  Rr = PHOTOCELL [package=photocell-kit]
  Rl = PHOTOCELL [package=photocell-kit]
  Ro = PHOTOCELL [package=photocell-kit]
  Ru = PHOTOCELL [package=photocell]

nets:
  N1: l_u_+_o_r.pin1, Rl.P$1
  N2: l_u_+_o_r.pin2, Ru.P$2
  N3: l_u_+_o_r.pin3, Rr.P$1, Rl.P$2, Ro.P$1, Ru.P$1
  N4: l_u_+_o_r.pin4, Ro.P$2
  N5: l_u_+_o_r.pin5, Rr.P$2

notes:
  LDR Array
