# Fritzing sketch SolarTracker-v2 (saved by Fritzing 1.0.1rc)
circuit board: 5.49978cm x 3.93717cm
breadboards: 1

parts:
  scl_sca_vcc_gnd = Grove OLED 128x96
  Nano = Arduino Nano (Rev3.0)
  MV = Dagu DGServo 9g header (male) [package=THT]
  MH = Dagu DGServo 9g header (male) [package=THT]
  10k = Resistor [tolerance=±5% resistance=10k power=0.25W package=THT]
  10k_2 = Resistor [tolerance=±5% resistance=10k power=0.25W package=THT]
  10k_3 = Resistor [tolerance=±5% resistance=10k power=0.25W package=THT]
  10k_4 = Resistor [tolerance=±5% resistance=10k power=0.25W package=THT]
  -_+ = Screw terminal - 2 pins [package=THT]
  o_u_l_r_+ = female pin header, 5 pins [form="♀ (female)"]
  J2C = female pin header, 2 pins [form="♀ (female)"]
  5_4_3_2 = female pin header, 4 pins [form="♀ (female)"]
  I2C = female pin header, 2 pins [form="♀ (female)"]

nets:
  GND: scl_sca_vcc_gnd.GND, Nano.GND, MV.gnd, MH.gnd, 10k.Pin_0, 10k_2.Pin_0, 10k_3.Pin_0, 10k_4.Pin_0, -_+.pin1
  VCC: scl_sca_vcc_gnd.VCC, Nano.5V, o_u_l_r_+.pin5
  N1: scl_sca_vcc_gnd.SDA, Nano.A4, J2C.pin1, I2C.pin1
  N2: scl_sca_vcc_gnd.SCL, Nano.A5, J2C.pin2, I2C.pin2
  N3: Nano.D2, MV.pulse, 5_4_3_2.pin4
  N4: Nano.D3, MH.pulse, 5_4_3_2.pin3
  N5: Nano.D4, 5_4_3_2.pin2
  N6: Nano.D5, 5_4_3_2.pin1
  VCC_2: Nano.VIN, MV.Vcc, MH.Vcc, -_+.pin2
  N7: Nano.A3, 10k_4.Pin_1, o_u_l_r_+.pin4
  N8: Nano.A2, 10k_3.Pin_1, o_u_l_r_+.pin3
  N9: Nano.A1, 10k_2.Pin_1, o_u_l_r_+.pin2
  N10: Nano.A0, 10k.Pin_1, o_u_l_r_+.pin1

notes:
  Solartracker V2
